// Logisim project ALU.circ as structural Verilog
module HalfAdder (
  input  a,
  input  b,
  output sum,
  output carry
);

  xor XOR (sum, a, b);
  and OX (carry, a, b);

  // Notes on the sheet:
  //   Half Adder
endmodule

module FullAdder (
  input  a,
  input  b,
  input  c,
  output sum,
  output carry
);

  wire HalfAdder_2_carry, HalfAdder_carry, HalfAdder_sum;

  HalfAdder HalfAdder (.a(a), .b(b), .sum(HalfAdder_sum), .carry(HalfAdder_carry));
  HalfAdder HalfAdder_2 (.a(HalfAdder_sum), .b(c), .sum(sum), .carry(HalfAdder_2_carry));
  or or_1 (carry, HalfAdder_carry, HalfAdder_2_carry);

  // Notes on the sheet:
  //   FullAdder
endmodule

module Add16 (
  input  [15:0] In_A,
  input  [15:0] In_B,
  output [15:0] Out
);

  wire FullAdder_2_carry, FullAdder_3_carry, FullAdder_4_carry, FullAdder_5_carry, FullAdder_6_carry,
       FullAdder_7_carry, FullAdder_8_carry, FullAdder_9_carry, FullAdder_10_carry, FullAdder_11_carry,
       FullAdder_12_carry, FullAdder_13_carry, FullAdder_14_carry, FullAdder_carry, HalfAdder_carry;

  HalfAdder HalfAdder (.a(In_A[0]), .b(In_B[0]), .sum(Out[0]), .carry(HalfAdder_carry));
  FullAdder FullAdder (.a(In_A[1]), .b(In_B[1]), .c(HalfAdder_carry), .sum(Out[1]), .carry(FullAdder_carry));
  FullAdder FullAdder_2 (.a(In_A[2]), .b(In_B[2]), .c(FullAdder_carry), .sum(Out[2]), .carry(FullAdder_2_carry));
  FullAdder FullAdder_3 (.a(In_A[3]), .b(In_B[3]), .c(FullAdder_2_carry), .sum(Out[3]), .carry(FullAdder_3_carry));
  FullAdder FullAdder_4 (.a(In_A[4]), .b(In_B[4]), .c(FullAdder_3_carry), .sum(Out[4]), .carry(FullAdder_4_carry));
  FullAdder FullAdder_5 (.a(In_A[5]), .b(In_B[5]), .c(FullAdder_4_carry), .sum(Out[5]), .carry(FullAdder_5_carry));
  FullAdder FullAdder_6 (.a(In_A[6]), .b(In_B[6]), .c(FullAdder_5_carry), .sum(Out[6]), .carry(FullAdder_6_carry));
  FullAdder FullAdder_7 (.a(In_A[7]), .b(In_B[7]), .c(FullAdder_6_carry), .sum(Out[7]), .carry(FullAdder_7_carry));
  FullAdder FullAdder_8 (.a(In_A[8]), .b(In_B[8]), .c(FullAdder_7_carry), .sum(Out[8]), .carry(FullAdder_8_carry));
  FullAdder FullAdder_9 (.a(In_A[9]), .b(In_B[9]), .c(FullAdder_8_carry), .sum(Out[9]), .carry(FullAdder_9_carry));
  FullAdder FullAdder_10 (.a(In_A[10]), .b(In_B[10]), .c(FullAdder_9_carry), .sum(Out[10]), .carry(FullAdder_10_carry));
  FullAdder FullAdder_11 (
    .a(In_A[11]), .b(In_B[11]), .c(FullAdder_10_carry), .sum(Out[11]), .carry(FullAdder_11_carry));
  FullAdder FullAdder_12 (
    .a(In_A[12]), .b(In_B[12]), .c(FullAdder_11_carry), .sum(Out[12]), .carry(FullAdder_12_carry));
  FullAdder FullAdder_13 (
    .a(In_A[13]), .b(In_B[13]), .c(FullAdder_12_carry), .sum(Out[13]), .carry(FullAdder_13_carry));
  FullAdder FullAdder_14 (
    .a(In_A[14]), .b(In_B[14]), .c(FullAdder_13_carry), .sum(Out[14]), .carry(FullAdder_14_carry));
  FullAdder FullAdder_15 (.a(In_A[15]), .b(In_B[15]), .c(FullAdder_14_carry), .sum(Out[15]));  // open: carry
endmodule

module And (
  input  a,
  input  b,
  output out
);

  wire nand_1_out;

  nand nand_1 (nand_1_out, a, b);
  not not_1 (out, nand_1_out);

  // Notes on the sheet:
  //   And
endmodule

module Not (
  input  a,
  input  b,
  output out
);

  nand nand_1 (out, a, b);

  // Notes on the sheet:
  //   Not
endmodule

module Or (
  input  a,
  input  b,
  output out
);

  wire and_1_out, not_1_out, not_2_out;

  not not_1 (not_1_out, a);
  not not_2 (not_2_out, b);
  and and_1 (and_1_out, not_1_out, not_2_out);
  not not_3 (out, and_1_out);

  // Notes on the sheet:
  //   Or
endmodule

module XOr (
  input  a,
  input  b,
  output out
);

  wire and_1_out, and_2_out, not_1_out, not_2_out;

  not not_1 (not_1_out, b);
  not not_2 (not_2_out, a);
  and and_1 (and_1_out, a, not_1_out);
  and and_2 (and_2_out, not_2_out, b);
  or or_1 (out, and_1_out, and_2_out);

  // Notes on the sheet:
  //   XOr
endmodule

module Mux (
  input  sel,
  input  a,
  input  b,
  output out
);

  wire and_1_out, and_2_out, not_1_out;

  not not_1 (not_1_out, sel);
  and and_1 (and_1_out, not_1_out, a);
  and and_2 (and_2_out, sel, b);
  xor xor_1 (out, and_1_out, and_2_out);

  // Notes on the sheet:
  //   Mux
endmodule

module DMux (
  input  sel,
  input  in,
  output a,
  output b
);

  wire not_1_out, or_1_out;

  not not_1 (not_1_out, in);
  not not_2 (a, or_1_out);
  or or_1 (or_1_out, sel, not_1_out);
  xor xor_1 (b, a, in);

  // Notes on the sheet:
  //   Dmux
endmodule

module And16 (
  input  [15:0] a,
  input  [15:0] b,
  output [15:0] out
);

  and and_1 (out[0], a[0], b[0]);
  and and_2 (out[1], a[1], b[1]);
  and and_3 (out[2], a[2], b[2]);
  and and_4 (out[3], a[3], b[3]);
  and and_5 (out[4], a[4], b[4]);
  and and_6 (out[5], a[5], b[5]);
  and and_7 (out[6], a[6], b[6]);
  and and_8 (out[7], a[7], b[7]);
  and and_9 (out[8], a[8], b[8]);
  and and_10 (out[9], a[9], b[9]);
  and and_11 (out[10], a[10], b[10]);
  and and_12 (out[11], a[11], b[11]);
  and and_13 (out[12], a[12], b[12]);
  and and_14 (out[13], a[13], b[13]);
  and and_15 (out[14], a[14], b[14]);
  and and_16 (out[15], a[15], b[15]);

  // Notes on the sheet:
  //   And16
endmodule

module Or8Way (
);

  ROM #(.addrWidth(16), .dataWidth(1)) rom_1 ();  // open: addr, data, sel

  // Notes on the sheet:
  //   contents of rom_1 (hex, n*v repeats v):
  //   0 1 4*0 1 0 0 0 1 7*0 1 0 0 1 4*0 1 0 0 1 15*0 1 12*0 1 12*0 1 0 1 9*0 1 9*0 1 9*0 1 0 0 0 1 11*0 1
  //   12*0 1 5*0 1 26*0 1
endmodule
