// Logisim project HACK-elements-TECS-lib.circ as structural Verilog: 27 circuits, main circuit gallery
module gallery (
);

  Mux mux_1 ();  // open: a, b, out, sel, sel_2
  Or8Way or8way_1 ();  // open: in, out
  HalfAdder halfadder_1 ();  // open: a, b, sum, carry
  DFF dff_1 ();  // open: in, out
  Mux16 mux16_1 ();  // open: a, b, out, sel, sel_2
  DMux dmux_1 ();  // open: in, a, b, sel, sel_2
  FullAdder fulladder_1 ();  // open: a, b, c, sum, carry
  Bit bit_1 ();  // open: in, out, load
  RAM8 ram8_1 ();  // open: in, address, out, load
  ALU alu_1 ();  // open: x, y, out, zx, nx, zy, ny, f, no, zr, ng
  CPU cpu_1 ();  // open: inM, instruction, reset, outM, writeM, addressM, pc
  Screen screen_1 ();  // open: in, address, out, load
  Mux4Way16 mux4way16_1 ();  // open: a, b, c, d, out, sel, sel_2
  DMux4Way dmux4way_1 ();  // open: in, a, b, c, d, sel, sel_2
  Add16 add16_1 ();  // open: a, b, out
  Register register_1 ();  // open: in, out, load
  RAM64 ram64_1 ();  // open: in, address, out, load
  Memory memory_1 ();  // open: in, address, out, load
  Keyboard keyboard_1 ();  // open: out
  Mux8Way16 mux8way16_1 ();  // open: a, b, c, d, e, f, g, h, out, sel, sel_2
  DMux8Way dmux8way_1 ();  // open: in, a, b, c, d, e, f, g, h, sel, sel_2
  Inc16 inc16_1 ();  // open: in, out
  RAM16K ram16k_1 ();  // open: in, address, out, load
  PC pc_1 ();  // open: in, out, inc, load, reset
  ROM32K rom32k_1 ();  // open: address, out

  // Notes on the sheet:
  //   Component Library for 
  //   The Elements of Computing Systems
  //   (From Nand to Tetris)
  //   Version 1.02
  //   e-mail: mark.armbrust@pobox.com
  //   These chips are implemented as wrappers around Logisim's
  //   built-in chips with similar functionality.  They don't show how
  //   to build the chips in HDL!
  //   Parts below ALU and PC are non-functional, except Screen
  //   which is implemented as an 8K RAM.
endmodule

module Or8Way (
  input  [7:0] in,
  output out
);

  or or_1 (out, in[0], in[1], in[2], in[3], in[4], in[5], in[6], in[7]);
endmodule

module Mux (
  input  sel,
  input  a,
  input  b,
  input  sel_2,
  output out
);

  Multiplexer #(.enable("false")) multiplexer_1 (.in0(a), .in1(b), .out(out), .sel(sel));

  assign sel_2 = sel;
endmodule

module Mux16 (
  input  sel,
  input  [15:0] a,
  input  [15:0] b,
  input  sel_2,
  output [15:0] out
);

  Multiplexer #(.width(16), .enable("false")) multiplexer_1 (.in0(a), .in1(b), .out(out), .sel(sel));

  assign sel_2 = sel;
endmodule

module Mux4Way16 (
  input  [15:0] a,
  input  [1:0] sel,
  input  [15:0] b,
  input  [15:0] c,
  input  [1:0] sel_2,
  input  [15:0] d,
  output [15:0] out
);

  Multiplexer #(.select(2), .width(16), .enable("false")) multiplexer_1 (
    .in0(a), .in1(b), .in2(c), .in3(d), .out(out), .sel(sel));

  assign sel_2 = sel;
endmodule

module Mux8Way16 (
  input  [15:0] a,
  input  [15:0] b,
  input  [2:0] sel,
  input  [15:0] c,
  input  [15:0] d,
  input  [15:0] e,
  input  [15:0] f,
  input  [2:0] sel_2,
  input  [15:0] g,
  input  [15:0] h,
  output [15:0] out
);

  Multiplexer #(.select(3), .width(16), .enable("false")) multiplexer_1 (
    .in0(a), .in1(b), .in2(c), .in3(d), .in4(e), .in5(f), .in6(g), .in7(h), .out(out), .sel(sel));

  assign sel_2 = sel;
endmodule

module DMux (
  input  sel,
  input  in,
  input  sel_2,
  output a,
  output b
);

  Demultiplexer #(.enable("false")) demultiplexer_1 (.out0(a), .out1(b), .in(in), .sel(sel));

  assign sel_2 = sel;
endmodule

module DMux4Way (
  input  [1:0] sel,
  input  in,
  input  [1:0] sel_2,
  output a,
  output b,
  output c,
  output d
);

  Demultiplexer #(.select(2), .enable("false")) demultiplexer_1 (
    .out0(a), .out1(b), .out2(c), .out3(d), .in(in), .sel(sel));

  assign sel_2 = sel;
endmodule

module DMux8Way (
  input  [2:0] sel,
  input  in,
  input  [2:0] sel_2,
  output a,
  output b,
  output c,
  output d,
  output e,
  output f,
  output g,
  output h
);

  Demultiplexer #(.select(3), .enable("false")) demultiplexer_1 (
    .out0(a), .out1(b), .out2(c), .out3(d), .out4(e), .out5(f), .out6(g), .out7(h), .in(in), .sel(sel));

  assign sel_2 = sel;
endmodule

module HalfAdder (
  input  a,
  input  b,
  output sum,
  output carry
);

  Adder #(.width(1)) adder_1 (.a(a), .b(b), .out(sum), .cout(carry));  // open: cin
endmodule

module FullAdder (
  input  a,
  input  b,
  input  c,
  output sum,
  output carry
);

  Adder #(.width(1)) adder_1 (.a(b), .b(c), .out(sum), .cin(a), .cout(carry));
endmodule

module Add16 (
  input  [15:0] a,
  input  [15:0] b,
  output [15:0] out
);

  Adder #(.width(16)) adder_1 (.a(a), .b(b), .out(out));  // open: cin, cout
endmodule

module Inc16 (
  input  [15:0] in,
  output [15:0] out
);

  Subtractor #(.width(16)) subtractor_1 (.a(in), .b({16{1'b1}}), .out(out));  // open: bin, bout
endmodule

module ALU (
  input  [15:0] x,
  input  zx,
  input  nx,
  input  zy,
  input  ny,
  input  f,
  input  no,
  input  [15:0] y,
  output [15:0] out,
  output zr,
  output ng
);

  wire a4_1_cyo, a4_1_f_2, a4_1_no_2, a4_1_nx_2, a4_1_ny_2, a4_1_zro, a4_1_zx_2, a4_1_zy_2, a4_2_cyo,
       a4_2_f_2, a4_2_no_2, a4_2_nx_2, a4_2_ny_2, a4_2_zro, a4_2_zx_2, a4_2_zy_2, a4_3_cyo, a4_3_f_2,
       a4_3_no_2, a4_3_nx_2, a4_3_ny_2, a4_3_zro, a4_3_zx_2, a4_3_zy_2;

  a4 a4_1 (
    .x(x[3:0]), .y(y[3:0]), .out(out[3:0]), .zx(zx), .nx(nx), .zy(zy), .ny(ny), .f(f), .no(no), .cyi(1'b0),
    .zri(1'b1), .zx_2(a4_1_zx_2), .nx_2(a4_1_nx_2), .zy_2(a4_1_zy_2), .ny_2(a4_1_ny_2), .f_2(a4_1_f_2),
    .no_2(a4_1_no_2), .cyo(a4_1_cyo), .zro(a4_1_zro));
  a4 a4_2 (
    .x(x[7:4]), .y(y[7:4]), .out(out[7:4]), .zx(a4_1_zx_2), .nx(a4_1_nx_2), .zy(a4_1_zy_2), .ny(a4_1_ny_2),
    .f(a4_1_f_2), .no(a4_1_no_2), .cyi(a4_1_cyo), .zri(a4_1_zro), .zx_2(a4_2_zx_2), .nx_2(a4_2_nx_2),
    .zy_2(a4_2_zy_2), .ny_2(a4_2_ny_2), .f_2(a4_2_f_2), .no_2(a4_2_no_2), .cyo(a4_2_cyo), .zro(a4_2_zro));
  a4 a4_3 (
    .x(x[11:8]), .y(y[11:8]), .out(out[11:8]), .zx(a4_2_zx_2), .nx(a4_2_nx_2), .zy(a4_2_zy_2),
    .ny(a4_2_ny_2), .f(a4_2_f_2), .no(a4_2_no_2), .cyi(a4_2_cyo), .zri(a4_2_zro), .zx_2(a4_3_zx_2),
    .nx_2(a4_3_nx_2), .zy_2(a4_3_zy_2), .ny_2(a4_3_ny_2), .f_2(a4_3_f_2), .no_2(a4_3_no_2), .cyo(a4_3_cyo),
    .zro(a4_3_zro));
  a4 a4_4 (
    .x(x[15:12]), .y(y[15:12]), .out({ng, out[14:12]}), .zx(a4_3_zx_2), .nx(a4_3_nx_2), .zy(a4_3_zy_2),
    .ny(a4_3_ny_2), .f(a4_3_f_2), .no(a4_3_no_2), .cyi(a4_3_cyo), .zri(a4_3_zro), .zro(zr));  // open: zx_2, nx_2, zy_2, ny_2, f_2, no_2, cyo

  assign out[15] = ng;
endmodule

module DFF (
  input  in,
  output out
);

  wire clock_1_out;

  Clock clock_1 (.out(clock_1_out));
  D_Flip_Flop d_ff_1 (.clk(clock_1_out), .D(in), .Q(out));  // open: Qn, preset, en, reset
endmodule

module Bit (
  input  load,
  input  in,
  output out
);

  wire clock_1_out;

  Register_part #(.width(1)) register_1 (.D(in), .en(load), .Q(out), .clk(clock_1_out));  // open: clr
  Clock clock_1 (.out(clock_1_out));
endmodule

module Register (
  input  load,
  input  [15:0] in,
  output [15:0] out
);

  wire clock_1_out;

  Clock clock_1 (.out(clock_1_out));
  Register_part #(.width(16)) register_1 (.D(in), .en(load), .Q(out), .clk(clock_1_out));  // open: clr
endmodule

module RAM8 (
  input  load,
  input  [15:0] in,
  input  [2:0] address,
  output [15:0] out
);

  wire clock_1_out;

  Clock clock_1 (.out(clock_1_out));
  RAM #(.addrWidth(3), .dataWidth(16), .bus("separate")) ram_1 (
    .addr(address), .din(in), .data(out), .str(load), .clk(clock_1_out));  // open: sel, ld, clr
endmodule

module RAM64 (
  input  load,
  input  [15:0] in,
  input  [5:0] address,
  output [15:0] out
);

  wire clock_1_out;

  Clock clock_1 (.out(clock_1_out));
  RAM #(.addrWidth(6), .dataWidth(16), .bus("separate")) ram_1 (
    .addr(address), .din(in), .data(out), .str(load), .clk(clock_1_out));  // open: sel, ld, clr
endmodule

module RAM16K (
  input  load,
  input  [15:0] in,
  input  [13:0] address,
  output [15:0] out
);

  wire clock_1_out;

  Clock clock_1 (.out(clock_1_out));
  RAM #(.addrWidth(14), .dataWidth(16), .bus("separate")) ram_1 (
    .addr(address), .din(in), .data(out), .str(load), .clk(clock_1_out));  // open: sel, ld, clr
endmodule

module PC (
  input  inc,
  input  load,
  input  reset,
  input  [15:0] in,
  output [15:0] out
);

  wire and_1_out, clock_1_out, or_1_out;
  wire [15:0] and_2_out, bit_extender_1_out;

  or or_1 (or_1_out, reset, load);
  assign bit_extender_1_out = {{15{reset}}, reset};  // Bit_Extender bit_extender_1
  Counter #(.width(16), .max('hffff)) counter_1 (
    .load(or_1_out), .D(and_2_out), .count(and_1_out), .Q(out), .clk(clock_1_out));  // open: carry, clr
  and and_1 (and_1_out, ~or_1_out, inc);  // AND_Gate
  Clock clock_1 (.out(clock_1_out));
  assign and_2_out = ~bit_extender_1_out & in;  // AND_Gate and_2, 16 bits wide
endmodule

module CPU (
  input  [15:0] inM,
  input  [15:0] instruction,
  input  reset,
  output [15:0] outM,
  output writeM,
  output [14:0] addressM,
  output [14:0] pc
);


  assign addressM = {15{1'b0}};
  assign outM = {16{1'b0}};
  assign pc = {15{1'b0}};
  assign writeM = 1'b0;
endmodule

module Memory (
  input  [15:0] in,
  input  load,
  input  [14:0] address,
  output [15:0] out
);


  assign out = {16{1'b0}};
endmodule

module ROM32K (
  input  [14:0] address,
  output [15:0] out
);


  assign out = {16{1'b0}};
endmodule

module Screen (
  input  load,
  input  [15:0] in,
  input  [12:0] address,
  output [15:0] out
);

  wire clock_1_out;

  Clock clock_1 (.out(clock_1_out));
  RAM #(.addrWidth(13), .dataWidth(16), .bus("separate")) ram_1 (
    .addr(address), .din(in), .data(out), .str(load), .clk(clock_1_out));  // open: sel, ld, clr
endmodule

module Keyboard (
  output [15:0] out
);


  assign out = {16{1'b0}};
endmodule

// 4-bit ALU
module a4 (
  input  zx,
  input  nx,
  input  zy,
  input  ny,
  input  f,
  input  no,
  input  cyi,
  input  zri,
  input  [3:0] x,
  input  [3:0] y,
  output [3:0] out,
  output cyo,
  output zro,
  output zx_2,
  output nx_2,
  output zy_2,
  output ny_2,
  output f_2,
  output no_2
);

  ROM #(.addrWidth(16), .dataWidth(6)) rom_1 (
    .addr({x, y, zx, nx, zy, ny, f, no, cyi, zri}), .data({out, cyo, zro}));  // open: sel

  assign f_2 = f;
  assign no_2 = no;
  assign nx_2 = nx;
  assign ny_2 = ny;
  assign zx_2 = zx;
  assign zy_2 = zy;

  // Notes on the sheet:
  //   contents of rom_1 (hex, n*v repeats v):
  //   0 1 0 1 4*3c 0 1 4 4 3c 3c 38 38 0 1 2 3 3c 3c 3e 3e 3c 3c 2 3 0 1 3e 3e 0 1 0 1 4*3c 0 1 4 4 3c 3c
  //   38 38 0 1 2 3 3c 3c 3e 3e 3c 3c 2 3 0 1 3e 3e 0 1 2 3 3c 3c 3e 3e 3c 3c 2 3 0 1 6*3e 2 3 2 3 3a 3a
  //   3e 3e 6 6 2 3 0 1 2 3 3c 3c 3e 3e 3c 3c 2 3 0 1 6*3e 2 3 2 3 3a 3a 3e 3e 6 6 2 3 0 1 0 1 4*3c 0 1 4
  //   4 3c 3c 38 38 0 1 2 3 3c 3c 3e 3e 3c 3c 2 3 0 1 3e 3e 0 1 0 1 4*3c 0 1 4 4 3c 3c 38 38 0 1 2 3 3c 3c
  //   3e 3e 3c 3c 2 3 0 1 3e 3e 0 1 2 3 3c 3c 3e 3e 3c 3c 2 3 0 1 6*3e 2 3 2 3 3a 3a 3e 3e 6 6 2 3 0 1 2 3
  //   3c 3c 3e 3e 3c 3c 2 3 0 1 6*3e 2 3 2 3 3a 3a 3e 3e 6 6 2 3 0 1 0 1 4*3c 4 4 8 8 38 38 34 34 0 1 0 1
  //   4*3c 38 38 3c 3c 4 4 0 1 0 1 0 1 4*3c 0 1 4 4 3c 3c 38 38 0 1 2 3 3c 3c 3e 3e 3c 3c 2 3 0 1 3e 3e
  //   4*6 4*3a 2 3 6 6 3e 3e 6*3a 4*6 36 36 3a 3a a a 6 6 0 1 2 3 3c 3c 3e 3e 3c 3c 2 3 0 1 6*3e 2 3 2 3
  //   3a 3a 3e 3e 6 6 2 3 0 1 0 1 4*3c 4 4 8 8 38 38 34 34 0 1 0 1 4*3c 38 38 3c 3c 4 4 0 1 0 1 0 1 4*3c 0
  //   1 4 4 3c 3c 38 38 0 1 2 3 3c 3c 3e 3e 3c 3c 2 3 0 1 3e 3e 4*6 4*3a 2 3 6 6 3e 3e 6*3a 4*6 36 36 3a
  //   3a a a 6 6 0 1 2 3 3c 3c 3e 3e 3c 3c 2 3 0 1 6*3e 2 3 2 3 3a 3a 3e 3e 6 6 2 3 0 1 0 1 4*3c 8 8 c c
  //   34 34 30 30 0 1 0 1 4*3c 34 34 38 38 8 8 4 4 0 1 0 1 4*3c 0 1 4 4 3c 3c 38 38 0 1 2 3 3c 3c 3e 3e 3c
  //   3c 2 3 0 1 3e 3e 4*a 4*36 6 6 a a 3a 3a 6*36 4*a 32 32 36 36 e e a a 0 1 2 3 3c 3c 3e 3e 3c 3c 2 3 0
  //   1 6*3e 2 3 2 3 3a 3a 3e 3e 6 6 2 3 0 1 0 1 4*3c 8 8 c c 34 34 30 30 0 1 0 1 4*3c 34 34 38 38 8 8 4 4
  //   0 1 0 1 4*3c 0 1 4 4 3c 3c 38 38 0 1 2 3 3c 3c 3e 3e 3c 3c 2 3 0 1 3e 3e 4*a 4*36 6 6 a a 3a 3a 6*36
  //   4*a 32 32 36 36 e e a a 0 1 2 3 3c 3c 3e 3e 3c 3c 2 3 0 1 6*3e 2 3 2 3 3a 3a 3e 3e 6 6 2 3 0 1 0 1
  //   4*3c c c 10 10 30 30 2c 2c 0 1 0 1 4*3c 30 30 34 34 c c 8 8 0 1 0 1 4*3c 0 1 4 4 3c 3c 38 38 0 1 2 3
  //   3c 3c 3e 3e 3c 3c 2 3 0 1 3e 3e 4*e 4*32 a a e e 36 36 6*32 4*e 2e 2e 32 32 12 12 e e 0 1 2 3 3c 3c
  //   3e 3e 3c 3c 2 3 0 1 6*3e 2 3 2 3 3a 3a 3e 3e 6 6 2 3 0 1 0 1 4*3c c c 10 10 30 30 2c 2c 0 1 0 1 4*3c
  //   30 30 34 34 c c 8 8 0 1 0 1 4*3c 0 1 4 4 3c 3c 38 38 0 1 2 3 3c 3c 3e 3e 3c 3c 2 3 0 1 3e 3e 4*e
  //   4*32 a a e e 36 36 6*32 4*e 2e 2e 32 32 12 12 e e 0 1 2 3 3c 3c 3e 3e 3c 3c 2 3 0 1 6*3e 2 3 2 3 3a
  //   3a 3e 3e 6 6 2 3 0 1 0 1 4*3c 10 10 14 14 2c 2c 28 28 0 1 0 1 4*3c 2c 2c 30 30 10 10 c c 0 1 0 1
  //   4*3c 0 1 4 4 3c 3c 38 38 0 1 2 3 3c 3c 3e 3e 3c 3c 2 3 0 1 3e 3e 4*12 4*2e e e 12 12 32 32 6*2e 4*12
  //   2a 2a 2e 2e 16 16 12 12 0 1 2 3 3c 3c 3e 3e 3c 3c 2 3 0 1 6*3e 2 3 2 3 3a 3a 3e 3e 6 6 2 3 0 1 0 1
  //   4*3c 10 10 14 14 2c 2c 28 28 0 1 0 1 4*3c 2c 2c 30 30 10 10 c c 0 1 0 1 4*3c 0 1 4 4 3c 3c 38 38 0 1
  //   2 3 3c 3c 3e 3e 3c 3c 2 3 0 1 3e 3e 4*12 4*2e e e 12 12 32 32 6*2e 4*12 2a 2a 2e 2e 16 16 12 12 0 1
  //   2 3 3c 3c 3e 3e 3c 3c 2 3 0 1 6*3e 2 3 2 3 3a 3a 3e 3e 6 6 2 3 0 1 0 1 4*3c 14 14 18 18 28 28 24 24
  //   0 1 0 1 4*3c 28 28 2c 2c 14 14 10 10 0 1 0 1 4*3c 0 1 4 4 3c 3c 38 38 0 1 2 3 3c 3c 3e 3e 3c 3c 2 3
  //   0 1 3e 3e 4*16 4*2a 12 12 16 16 2e 2e 6*2a 4*16 26 26 2a 2a 1a 1a 16 16 0 1 2 3 3c 3c 3e 3e 3c 3c 2
  //   3 0 1 6*3e 2 3 2 3 3a 3a 3e 3e 6 6 2 3 0 1 0 1 4*3c 14 14 18 18 28 28 24 24 0 1 0 1 4*3c 28 28 2c 2c
  //   14 14 10 10 0 1 0 1 4*3c 0 1 4 4 3c 3c 38 38 0 1 2 3 3c 3c 3e 3e 3c 3c 2 3 0 1 3e 3e 4*16 4*2a 12 12
  //   16 16 2e 2e 6*2a 4*16 26 26 2a 2a 1a 1a 16 16 0 1 2 3 3c 3c 3e 3e 3c 3c 2 3 0 1 6*3e 2 3 2 3 3a 3a
  //   3e 3e 6 6 2 3 0 1 0 1 4*3c 18 18 1c 1c 24 24 20 20 0 1 0 1 4*3c 24 24 28 28 18 18 14 14 0 1 0 1 4*3c
  //   0 1 4 4 3c 3c 38 38 0 1 2 3 3c 3c 3e 3e 3c 3c 2 3 0 1 3e 3e 4*1a 4*26 16 16 1a 1a 2a 2a 6*26 4*1a 22
  //   22 26 26 1e 1e 1a 1a 0 1 2 3 3c 3c 3e 3e 3c 3c 2 3 0 1 6*3e 2 3 2 3 3a 3a 3e 3e 6 6 2 3 0 1 0 1 4*3c
  //   18 18 1c 1c 24 24 20 20 0 1 0 1 4*3c 24 24 28 28 18 18 14 14 0 1 0 1 4*3c 0 1 4 4 3c 3c 38 38 0 1 2
  //   3 3c 3c 3e 3e 3c 3c 2 3 0 1 3e 3e 4*1a 4*26 16 16 1a 1a 2a 2a 6*26 4*1a 22 22 26 26 1e 1e 1a 1a 0 1
  //   2 3 3c 3c 3e 3e 3c 3c 2 3 0 1 6*3e 2 3 2 3 3a 3a 3e 3e 6 6 2 3 0 1 0 1 4*3c 1c 1c 4*20 1c 1c 0 1 0 1
  //   4*3c 20 20 24 24 1c 1c 18 18 0 1 0 1 4*3c 0 1 4 4 3c 3c 38 38 0 1 2 3 3c 3c 3e 3e 3c 3c 2 3 0 1 3e
  //   3e 4*1e 4*22 1a 1a 1e 1e 26 26 6*22 6*1e 4*22 1e 1e 0 1 2 3 3c 3c 3e 3e 3c 3c 2 3 0 1 6*3e 2 3 2 3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
endmodule
