// Logisim project HACK_CPU.circ as structural Verilog: 23 circuits, main circuit CPU
module ALU (
  input  in_1,
  input  in_2,
  input  in_3,
  input  in_4,
  input  in_5,
  input  in_6,
  input  [15:0] D,
  input  [15:0] A,
  output [15:0] out_9,
  output out_10,
  output out_11,
  output out_12
);

  wire not_1_out;
  wire [15:0] adder_1_out, and16_1_out, bitselector_1_out, bitselector_2_out, bitselector_3_out,
       bitselector_4_out, not16_1_out, not16_2_out, or_1_out;

  Not16 not16_1 (.out(not16_1_out));  // open: in
  BitSelector #(.width(16), .group(16)) bitselector_1 (.in(D), .out(bitselector_1_out), .sel(in_1));
  FullAdder fulladder_1 ();  // open: a, b, c, sum, carry
  Not16 not16_2 (.out(not16_2_out));  // open: in
  BitSelector #(.width(16), .group(16)) bitselector_2 (.in(A), .out(bitselector_2_out), .sel(in_3));
  Adder #(.width(16)) adder_1 (.a(not16_1_out), .b(not16_2_out), .out(adder_1_out));  // open: cin, cout
  BitSelector #(.width(16), .group(16)) bitselector_3 (.in(adder_1_out), .out(bitselector_3_out), .sel(not_1_out));
  And16 and16_1 (.out(and16_1_out), .a(not16_1_out), .b(not16_2_out));
  BitSelector #(.width(16), .group(16)) bitselector_4 (.in(and16_1_out), .out(bitselector_4_out), .sel(in_5));
  not not_1 (not_1_out, in_5);
  assign or_1_out = bitselector_3_out | bitselector_4_out;  // OR_Gate or_1, 16 bits wide
  Not16 not16_3 (.out(out_9));  // open: in
  Comparator #(.width(16)) comparator_1 (.a(out_9), .b({16{1'b0}}), .gt(out_10), .eq(out_11), .lt(out_12));
endmodule

module Computer (
  input  in_1,
  input  in_2,
  input  [15:0] in_3,
  input  in_4
);

  wire clock_1_out, cpu_1_out_20, cpu_1_out_22, not_1_out, not_2_out, not_3_out;
  wire [3:0] ram_1_data_2;
  wire [11:0] ram_1_data;
  wire [14:0] or_1_out_2;
  wire [15:0] bitselector_1_out, bitselector_2_out, counter_1_q, cpu_1_out_19, cpu_1_out_21, cpu_1_outm,
       rom_1_data;
  wire [15:15] or_1_out;

  not not_1 (not_1_out, or_1_out[15]);
  BitSelector #(.width(16), .group(16)) bitselector_1 (
    .in({or_1_out[15], or_1_out_2}), .out(bitselector_1_out), .sel(not_1_out));
  Clock clock_1 (.out(clock_1_out));
  assign {or_1_out[15], or_1_out_2} = in_3 | bitselector_2_out;  // OR_Gate or_1, 16 bits wide
  CPU cpu_1 (
    .Instruction({1'b0, or_1_out_2}), .inM({ram_1_data_2, ram_1_data}), .outM(cpu_1_outm),
    .out_19(cpu_1_out_19), .out_20(cpu_1_out_20), .CLK(clock_1_out), .in_4(or_1_out[15]),
    .in_5(bitselector_1_out[12]), .in_6(bitselector_1_out[11]), .in_7(bitselector_1_out[10]),
    .in_8(bitselector_1_out[9]), .in_9(bitselector_1_out[8]), .in_10(bitselector_1_out[7]),
    .in_11(bitselector_1_out[6]), .in_12(bitselector_1_out[5]), .in_13(bitselector_1_out[4]),
    .in_14(bitselector_1_out[3]), .in_15(bitselector_1_out[2]), .in_16(bitselector_1_out[1]),
    .in_17(bitselector_1_out[0]), .out_21(cpu_1_out_21), .out_22(cpu_1_out_22));
  BitSelector #(.width(16), .group(16)) bitselector_2 (.in(rom_1_data), .out(bitselector_2_out), .sel(in_4));
  Hex_Digit_Display hex_digit_display_1 (.value(cpu_1_outm[15:12]));  // open: dp
  Counter #(.width(16), .max('hffff)) counter_1 (
    .load(cpu_1_out_20), .D(cpu_1_out_21), .count(not_2_out), .Q(counter_1_q), .clk(clock_1_out), .clr(in_2));  // open: carry
  not not_2 (not_2_out, cpu_1_out_20);
  Hex_Digit_Display hex_digit_display_2 (.value(cpu_1_outm[11:8]));  // open: dp
  Hex_Digit_Display hex_digit_display_3 (.value(cpu_1_outm[7:4]));  // open: dp
  Hex_Digit_Display hex_digit_display_4 (.value(cpu_1_outm[3:0]));  // open: dp
  ROM #(.addrWidth(16), .dataWidth(16)) rom_1 (.addr(counter_1_q), .data(rom_1_data), .sel(1'b1));
  Hex_Digit_Display hex_digit_display_5 (.value(ram_1_data[11:8]));  // open: dp
  Hex_Digit_Display hex_digit_display_6 (.value(ram_1_data_2));  // open: dp
  RAM #(.addrWidth(16), .dataWidth(16), .bus("separate")) ram_1 (
    .addr(cpu_1_out_19), .din(cpu_1_outm), .data({ram_1_data_2, ram_1_data}), .str(cpu_1_out_22), .sel(1'b1),
    .clk(clock_1_out), .ld(not_3_out), .clr(in_1));
  not not_3 (not_3_out, clock_1_out);
  Hex_Digit_Display hex_digit_display_7 (.value(ram_1_data[3:0]));  // open: dp
  Hex_Digit_Display hex_digit_display_8 (.value(ram_1_data[7:4]));  // open: dp

  // Notes on the sheet:
  //   16 Bit SemiRISC - CPU, 16 KB RAM + 8 KB VRAM + 2 Byte Keyboard, Memory-Mapped Devices
  //   32 KB ROM
  //   contents of rom_1 (hex, n*v repeats v):
  //   10 efc8 11 ea88 10 fc10 64 e4d0 12 e301 10 fc10 11 f088 10 fdc8 4 ea87 12 ea87
endmodule

module Not16 (
  input  [15:0] in,
  output [15:0] out
);

  not not_1 (out[15], in[15]);
  not not_2 (out[14], in[14]);
  not not_3 (out[13], in[13]);
  not not_4 (out[12], in[12]);
  not not_5 (out[11], in[11]);
  not not_6 (out[10], in[10]);
  not not_7 (out[9], in[9]);
  not not_8 (out[8], in[8]);
  not not_9 (out[7], in[7]);
  not not_10 (out[6], in[6]);
  not not_11 (out[5], in[5]);
  not not_12 (out[4], in[4]);
  not not_13 (out[3], in[3]);
  not not_14 (out[2], in[2]);
  not not_15 (out[1], in[1]);
  not not_16 (out[0], in[0]);
endmodule

module And16 (
  input  [15:0] a,
  input  [15:0] b,
  output [15:0] out
);

  and and_1 (out[15], a[15], b[15]);
  and and_2 (out[14], a[14], b[14]);
  and and_3 (out[13], a[13], b[13]);
  and and_4 (out[12], a[12], b[12]);
  and and_5 (out[11], a[11], b[11]);
  and and_6 (out[10], a[10], b[10]);
  and and_7 (out[9], a[9], b[9]);
  and and_8 (out[8], a[8], b[8]);
  and and_9 (out[7], a[7], b[7]);
  and and_10 (out[6], a[6], b[6]);
  and and_11 (out[5], a[5], b[5]);
  and and_12 (out[4], a[4], b[4]);
  and and_13 (out[3], a[3], b[3]);
  and and_14 (out[2], a[2], b[2]);
  and and_15 (out[1], a[1], b[1]);
  and and_16 (out[0], a[0], b[0]);
endmodule

module CPU (
  input  [15:0] Instruction,
  input  [15:0] inM,
  input  CLK,
  input  in_4,
  input  in_5,
  input  in_6,
  input  in_7,
  input  in_8,
  input  in_9,
  input  in_10,
  input  in_11,
  input  in_12,
  input  in_13,
  input  in_14,
  input  in_15,
  input  in_16,
  input  in_17,
  output [15:0] outM,
  output [15:0] out_19,
  output out_20,
  output [15:0] out_21,
  output out_22
);

  wire alu_1_out_10, alu_1_out_11, alu_1_out_12, and_1_out, and_2_out, and_3_out, bitselector_1_out,
       bitselector_2_out, not_1_out, not_2_out, or_1_out;
  wire [15:0] D_register_q, multiplexer_1_out, multiplexer_2_out;

  or or_1 (or_1_out, bitselector_1_out, bitselector_2_out);
  BitSelector #(.width(1)) bitselector_1 (.in(CLK), .out(bitselector_1_out), .sel(in_4));
  Multiplexer #(.width(16), .enable("false")) multiplexer_1 (
    .in0(outM), .in1(Instruction), .out(multiplexer_1_out), .sel(not_1_out));
  not not_1 (not_1_out, in_4);
  not not_2 (not_2_out, in_12);
  Register #(.width(16)) A_register (.D(multiplexer_1_out), .Q(out_19), .clk(or_1_out));  // open: en, clr
  BitSelector #(.width(1)) bitselector_2 (.in(CLK), .out(bitselector_2_out), .sel(not_2_out));
  Register #(.width(16)) D_register (.D(outM), .en(in_13), .Q(D_register_q), .clk(CLK));  // open: clr
  Multiplexer #(.width(16), .enable("false")) multiplexer_2 (
    .in0(out_19), .in1(inM), .out(multiplexer_2_out), .sel(in_5));
  ALU alu_1 (
    .out_9(outM), .in_1(in_6), .in_2(in_7), .in_3(in_8), .in_4(in_9), .in_5(in_10), .in_6(in_11),
    .D(D_register_q), .A(multiplexer_2_out), .out_10(alu_1_out_10), .out_11(alu_1_out_11),
    .out_12(alu_1_out_12));
  and and_1 (and_1_out, in_17, alu_1_out_10);
  and and_2 (and_2_out, in_16, alu_1_out_11);
  and and_3 (and_3_out, in_15, alu_1_out_12);
  or or_2 (out_20, and_1_out, and_2_out, and_3_out);

  assign out_21 = out_19;
  assign out_22 = in_14;

  // Notes on the sheet:
  //   inM
  //   A
  //   D
endmodule

module Not (
  input  in,
  output out
);

  nand NAND (out, in, in);
endmodule

module And (
  input  a,
  input  b,
  output out
);

  wire nand_1_out;

  nand nand_1 (nand_1_out, a, b);
  Not not_1 (.in(nand_1_out), .out(out));
endmodule

module Or (
  input  a,
  input  b,
  output out
);

  wire and_1_out, not_1_out, not_2_out;

  not not_1 (not_1_out, a);
  and and_1 (and_1_out, not_1_out, not_2_out);
  not not_2 (not_2_out, b);
  not not_3 (out, and_1_out);
endmodule

module Xor (
  input  a,
  input  b,
  output out
);

  wire and_2_out, and_out, not_a_out, not_b_out;

  not not_b (not_b_out, b);
  not not_a (not_a_out, a);
  and \and  (and_out, a, not_b_out);
  and and_2 (and_2_out, not_a_out, b);
  or or_1 (out, and_out, and_2_out);
endmodule

module Mux (
  input  sel,
  input  a,
  input  b,
  output out
);

  wire AND_2_out, AND_out, not_1_out;

  not not_1 (not_1_out, sel);
  and AND (AND_out, not_1_out, a);
  and AND_2 (AND_2_out, sel, b);
  xor XOR (out, AND_out, AND_2_out);
endmodule

module DMux (
  input  sel,
  input  in,
  output a,
  output b
);

  wire not_1_out, or_1_out;

  or or_1 (or_1_out, sel, not_1_out);
  not not_1 (not_1_out, in);
  not not_2 (a, or_1_out);
  xor xor_1 (b, a, in);
endmodule

module DMux4Way (
  input  [1:0] sel,
  input  in,
  output a,
  output b,
  output c,
  output d
);

  wire demultiplexer_1_out0, demultiplexer_1_out1;

  Demultiplexer #(.enable("false")) demultiplexer_1 (
    .out0(demultiplexer_1_out0), .out1(demultiplexer_1_out1), .in(in), .sel(sel[1]));
  Demultiplexer #(.enable("false")) demultiplexer_2 (.out0(a), .out1(b), .in(demultiplexer_1_out0), .sel(sel[0]));
  Demultiplexer #(.enable("false")) demultiplexer_3 (.out0(c), .out1(d), .in(demultiplexer_1_out1), .sel(sel[0]));
endmodule

module HalfAdder (
  input  a,
  input  b,
  output sum,
  output carry
);

  xor XOR (sum, a, b);
  and OX (carry, a, b);

  // Notes on the sheet:
  //   Half Adder
endmodule

module FullAdder (
  input  a,
  input  b,
  input  c,
  output sum,
  output carry
);

  wire HalfAdder_2_carry, HalfAdder_carry, HalfAdder_sum;

  HalfAdder HalfAdder (.a(a), .b(b), .sum(HalfAdder_sum), .carry(HalfAdder_carry));
  HalfAdder HalfAdder_2 (.a(HalfAdder_sum), .b(c), .sum(sum), .carry(HalfAdder_2_carry));
  or or_1 (carry, HalfAdder_carry, HalfAdder_2_carry);

  // Notes on the sheet:
  //   FullAdder
endmodule

module Inc16 (
  input  [15:0] in,
  output [15:0] out
);

  And16 and16_1 (.out(out), .a(in), .b({16{1'b1}}));
endmodule

module Add16 (
  input  [15:0] In_A,
  input  [15:0] In_B,
  output [15:0] Out
);

  wire FullAdder_2_carry, FullAdder_3_carry, FullAdder_4_carry, FullAdder_5_carry, FullAdder_6_carry,
       FullAdder_7_carry, FullAdder_8_carry, FullAdder_9_carry, FullAdder_10_carry, FullAdder_11_carry,
       FullAdder_12_carry, FullAdder_13_carry, FullAdder_14_carry, FullAdder_carry, HalfAdder_carry;

  HalfAdder HalfAdder (.a(In_A[0]), .b(In_B[0]), .sum(Out[0]), .carry(HalfAdder_carry));
  FullAdder FullAdder (.a(In_A[1]), .b(In_B[1]), .c(HalfAdder_carry), .sum(Out[1]), .carry(FullAdder_carry));
  FullAdder FullAdder_2 (.a(In_A[2]), .b(In_B[2]), .c(FullAdder_carry), .sum(Out[2]), .carry(FullAdder_2_carry));
  FullAdder FullAdder_3 (.a(In_A[3]), .b(In_B[3]), .c(FullAdder_2_carry), .sum(Out[3]), .carry(FullAdder_3_carry));
  FullAdder FullAdder_4 (.a(In_A[4]), .b(In_B[4]), .c(FullAdder_3_carry), .sum(Out[4]), .carry(FullAdder_4_carry));
  FullAdder FullAdder_5 (.a(In_A[5]), .b(In_B[5]), .c(FullAdder_4_carry), .sum(Out[5]), .carry(FullAdder_5_carry));
  FullAdder FullAdder_6 (.a(In_A[6]), .b(In_B[6]), .c(FullAdder_5_carry), .sum(Out[6]), .carry(FullAdder_6_carry));
  FullAdder FullAdder_7 (.a(In_A[7]), .b(In_B[7]), .c(FullAdder_6_carry), .sum(Out[7]), .carry(FullAdder_7_carry));
  FullAdder FullAdder_8 (.a(In_A[8]), .b(In_B[8]), .c(FullAdder_7_carry), .sum(Out[8]), .carry(FullAdder_8_carry));
  FullAdder FullAdder_9 (.a(In_A[9]), .b(In_B[9]), .c(FullAdder_8_carry), .sum(Out[9]), .carry(FullAdder_9_carry));
  FullAdder FullAdder_10 (.a(In_A[10]), .b(In_B[10]), .c(FullAdder_9_carry), .sum(Out[10]), .carry(FullAdder_10_carry));
  FullAdder FullAdder_11 (
    .a(In_A[11]), .b(In_B[11]), .c(FullAdder_10_carry), .sum(Out[11]), .carry(FullAdder_11_carry));
  FullAdder FullAdder_12 (
    .a(In_A[12]), .b(In_B[12]), .c(FullAdder_11_carry), .sum(Out[12]), .carry(FullAdder_12_carry));
  FullAdder FullAdder_13 (
    .a(In_A[13]), .b(In_B[13]), .c(FullAdder_12_carry), .sum(Out[13]), .carry(FullAdder_13_carry));
  FullAdder FullAdder_14 (
    .a(In_A[14]), .b(In_B[14]), .c(FullAdder_13_carry), .sum(Out[14]), .carry(FullAdder_14_carry));
  FullAdder FullAdder_15 (.a(In_A[15]), .b(In_B[15]), .c(FullAdder_14_carry), .sum(Out[15]));  // open: carry
endmodule

module Or16 (
  input  [15:0] a,
  input  [15:0] b,
  output [15:0] out
);

  assign out = a | b;  // OR_Gate or_1, 16 bits wide
endmodule

module Mux16 (
  input  sel,
  input  [15:0] a,
  input  [15:0] b,
  output [15:0] out
);

  Multiplexer #(.width(16), .enable("false")) multiplexer_1 (.in0(a), .in1(b), .out(out), .sel(sel));
endmodule

module Or8Way (
  input  [7:0] in,
  output out
);

  wire or_1_out, or_2_out, or_3_out, or_4_out, or_5_out, or_6_out;

  or or_1 (or_1_out, in[0], in[1]);
  or or_2 (or_2_out, or_1_out, in[2]);
  or or_3 (or_3_out, or_2_out, in[3]);
  or or_4 (or_4_out, or_3_out, in[4]);
  or or_5 (or_5_out, or_4_out, in[5]);
  or or_6 (or_6_out, or_5_out, in[6]);
  or or_7 (out, or_6_out, in[7]);
endmodule

module DMux8Way (
  input  [2:0] in_1,
  input  in,
  output a,
  output b,
  output c,
  output d,
  output e,
  output f,
  output g,
  output h
);

  Demultiplexer #(.select(3), .enable("false")) demultiplexer_1 (
    .out0(a), .out1(b), .out2(c), .out3(d), .out4(e), .out5(f), .out6(g), .out7(h), .in(in), .sel(in_1));
endmodule

module Mux4Way16 (
  input  [15:0] a,
  input  [15:0] b,
  input  [15:0] c,
  input  [1:0] sel,
  input  [15:0] d,
  output [15:0] out
);

  Multiplexer #(.select(2), .width(16), .enable("false")) multiplexer_1 (
    .in0(a), .in1(b), .in2(c), .in3(d), .out(out), .sel(sel));
endmodule

module Mux8Way16 (
  input  [15:0] a,
  input  [15:0] b,
  input  [15:0] c,
  input  [15:0] d,
  input  [15:0] e,
  input  [15:0] f,
  input  [2:0] sel,
  input  [15:0] g,
  input  [15:0] h,
  output [15:0] out
);

  Multiplexer #(.select(3), .width(16), .enable("false")) multiplexer_1 (
    .in0(a), .in1(b), .in2(c), .in3(d), .in4(e), .in5(f), .in6(g), .in7(h), .out(out), .sel(sel));
endmodule

module ALUMy (
  input  in_1,
  input  [15:0] x,
  input  [15:0] y,
  output [15:0] out
);

  wire [15:0] Mux16_out, Not16_2_out;

  Not16 Not16 ();  // open: out, in
  And16 And16 ();  // open: out, a, b
  Mux16 Mux16 (.a(x), .b({16{1'b0}}), .out(Mux16_out));  // open: sel
  Not16 Not16_2 (.out(Not16_2_out), .in(Mux16_out));
  Mux16 Mux16_2 (.a(Mux16_out), .b(Not16_2_out));  // open: out, sel
endmodule
