// Logisim project HACK_CPU_my.circ as structural Verilog
module Not16 (
  input  [15:0] in,
  output [15:0] out
);

  not not_1 (out[15], in[15]);
  not not_2 (out[14], in[14]);
  not not_3 (out[13], in[13]);
  not not_4 (out[12], in[12]);
  not not_5 (out[11], in[11]);
  not not_6 (out[10], in[10]);
  not not_7 (out[9], in[9]);
  not not_8 (out[8], in[8]);
  not not_9 (out[7], in[7]);
  not not_10 (out[6], in[6]);
  not not_11 (out[5], in[5]);
  not not_12 (out[4], in[4]);
  not not_13 (out[3], in[3]);
  not not_14 (out[2], in[2]);
  not not_15 (out[1], in[1]);
  not not_16 (out[0], in[0]);
endmodule

module And16 (
  input  [15:0] a,
  input  [15:0] b,
  output [15:0] out
);

  and and_1 (out[15], a[15], b[15]);
  and and_2 (out[14], a[14], b[14]);
  and and_3 (out[13], a[13], b[13]);
  and and_4 (out[12], a[12], b[12]);
  and and_5 (out[11], a[11], b[11]);
  and and_6 (out[10], a[10], b[10]);
  and and_7 (out[9], a[9], b[9]);
  and and_8 (out[8], a[8], b[8]);
  and and_9 (out[7], a[7], b[7]);
  and and_10 (out[6], a[6], b[6]);
  and and_11 (out[5], a[5], b[5]);
  and and_12 (out[4], a[4], b[4]);
  and and_13 (out[3], a[3], b[3]);
  and and_14 (out[2], a[2], b[2]);
  and and_15 (out[1], a[1], b[1]);
  and and_16 (out[0], a[0], b[0]);
endmodule

module Not (
  input  in,
  output out
);

  nand NAND (out, in, in);
endmodule

module And (
  input  a,
  input  b,
  output out
);

  wire nand_1_out;

  nand nand_1 (nand_1_out, a, b);
  Not not_1 (.in(nand_1_out), .out(out));
endmodule

module Or (
  input  a,
  input  b,
  output out
);

  wire and_1_out, not_1_out, not_2_out;

  not not_1 (not_1_out, a);
  and and_1 (and_1_out, not_1_out, not_2_out);
  not not_2 (not_2_out, b);
  not not_3 (out, and_1_out);
endmodule

module Xor (
  input  a,
  input  b,
  output out
);

  wire and_2_out, and_out, not_a_out, not_b_out;

  not not_b (not_b_out, b);
  not not_a (not_a_out, a);
  and \and  (and_out, a, not_b_out);
  and and_2 (and_2_out, not_a_out, b);
  or or_1 (out, and_out, and_2_out);
endmodule

module Mux (
  input  sel,
  input  a,
  input  b,
  output out
);

  wire AND_2_out, AND_out, not_1_out;

  not not_1 (not_1_out, sel);
  and AND (AND_out, not_1_out, a);
  and AND_2 (AND_2_out, sel, b);
  xor XOR (out, AND_out, AND_2_out);
endmodule

module DMux (
  input  sel,
  input  in,
  output a,
  output b
);

  wire not_1_out, or_1_out;

  or or_1 (or_1_out, sel, not_1_out);
  not not_1 (not_1_out, in);
  not not_2 (a, or_1_out);
  xor xor_1 (b, a, in);
endmodule

module DMux4Way (
  input  [1:0] sel,
  input  in,
  output a,
  output b,
  output c,
  output d
);

  wire demultiplexer_1_out0, demultiplexer_1_out1;

  Demultiplexer #(.enable("false")) demultiplexer_1 (
    .out0(demultiplexer_1_out0), .out1(demultiplexer_1_out1), .in(in), .sel(sel[1]));
  Demultiplexer #(.enable("false")) demultiplexer_2 (.out0(a), .out1(b), .in(demultiplexer_1_out0), .sel(sel[0]));
  Demultiplexer #(.enable("false")) demultiplexer_3 (.out0(c), .out1(d), .in(demultiplexer_1_out1), .sel(sel[0]));
endmodule

module HalfAdder (
  input  a,
  input  b,
  output sum,
  output carry
);

  xor XOR (sum, a, b);
  and OX (carry, a, b);

  // Notes on the sheet:
  //   Half Adder
endmodule

module FullAdder (
  input  a,
  input  b,
  input  c,
  output sum,
  output carry
);

  wire HalfAdder_2_carry, HalfAdder_carry, HalfAdder_sum;

  HalfAdder HalfAdder (.a(a), .b(b), .sum(HalfAdder_sum), .carry(HalfAdder_carry));
  HalfAdder HalfAdder_2 (.a(HalfAdder_sum), .b(c), .sum(sum), .carry(HalfAdder_2_carry));
  or or_1 (carry, HalfAdder_carry, HalfAdder_2_carry);

  // Notes on the sheet:
  //   FullAdder
endmodule

module Inc16 (
  input  [15:0] in,
  output [15:0] out
);

  Add16 Add16 (.In_A(in), .In_B({16{1'b1}}), .Out(out));
endmodule

module Add16 (
  input  [15:0] In_A,
  input  [15:0] In_B,
  output [15:0] Out
);

  wire FullAdder_2_carry, FullAdder_3_carry, FullAdder_4_carry, FullAdder_5_carry, FullAdder_6_carry,
       FullAdder_7_carry, FullAdder_8_carry, FullAdder_9_carry, FullAdder_10_carry, FullAdder_11_carry,
       FullAdder_12_carry, FullAdder_13_carry, FullAdder_14_carry, FullAdder_carry, HalfAdder_carry;

  HalfAdder HalfAdder (.a(In_A[0]), .b(In_B[0]), .sum(Out[0]), .carry(HalfAdder_carry));
  FullAdder FullAdder (.a(In_A[1]), .b(In_B[1]), .c(HalfAdder_carry), .sum(Out[1]), .carry(FullAdder_carry));
  FullAdder FullAdder_2 (.a(In_A[2]), .b(In_B[2]), .c(FullAdder_carry), .sum(Out[2]), .carry(FullAdder_2_carry));
  FullAdder FullAdder_3 (.a(In_A[3]), .b(In_B[3]), .c(FullAdder_2_carry), .sum(Out[3]), .carry(FullAdder_3_carry));
  FullAdder FullAdder_4 (.a(In_A[4]), .b(In_B[4]), .c(FullAdder_3_carry), .sum(Out[4]), .carry(FullAdder_4_carry));
  FullAdder FullAdder_5 (.a(In_A[5]), .b(In_B[5]), .c(FullAdder_4_carry), .sum(Out[5]), .carry(FullAdder_5_carry));
  FullAdder FullAdder_6 (.a(In_A[6]), .b(In_B[6]), .c(FullAdder_5_carry), .sum(Out[6]), .carry(FullAdder_6_carry));
  FullAdder FullAdder_7 (.a(In_A[7]), .b(In_B[7]), .c(FullAdder_6_carry), .sum(Out[7]), .carry(FullAdder_7_carry));
  FullAdder FullAdder_8 (.a(In_A[8]), .b(In_B[8]), .c(FullAdder_7_carry), .sum(Out[8]), .carry(FullAdder_8_carry));
  FullAdder FullAdder_9 (.a(In_A[9]), .b(In_B[9]), .c(FullAdder_8_carry), .sum(Out[9]), .carry(FullAdder_9_carry));
  FullAdder FullAdder_10 (.a(In_A[10]), .b(In_B[10]), .c(FullAdder_9_carry), .sum(Out[10]), .carry(FullAdder_10_carry));
  FullAdder FullAdder_11 (
    .a(In_A[11]), .b(In_B[11]), .c(FullAdder_10_carry), .sum(Out[11]), .carry(FullAdder_11_carry));
  FullAdder FullAdder_12 (
    .a(In_A[12]), .b(In_B[12]), .c(FullAdder_11_carry), .sum(Out[12]), .carry(FullAdder_12_carry));
  FullAdder FullAdder_13 (
    .a(In_A[13]), .b(In_B[13]), .c(FullAdder_12_carry), .sum(Out[13]), .carry(FullAdder_13_carry));
  FullAdder FullAdder_14 (
    .a(In_A[14]), .b(In_B[14]), .c(FullAdder_13_carry), .sum(Out[14]), .carry(FullAdder_14_carry));
  FullAdder FullAdder_15 (.a(In_A[15]), .b(In_B[15]), .c(FullAdder_14_carry), .sum(Out[15]));  // open: carry
endmodule

module Or16 (
  input  [15:0] a,
  input  [15:0] b,
  output [15:0] out
);

  assign out = a | b;  // OR_Gate or_1, 16 bits wide
endmodule

module Mux16 (
  input  sel,
  input  [15:0] a,
  input  [15:0] b,
  output [15:0] out
);

  Multiplexer #(.width(16), .enable("false")) multiplexer_1 (.in0(a), .in1(b), .out(out), .sel(sel));
endmodule

module Or8Way (
  input  [7:0] in,
  output out
);

  wire or_1_out, or_2_out, or_3_out, or_4_out, or_5_out, or_6_out;

  or or_1 (or_1_out, in[0], in[1]);
  or or_2 (or_2_out, or_1_out, in[2]);
  or or_3 (or_3_out, or_2_out, in[3]);
  or or_4 (or_4_out, or_3_out, in[4]);
  or or_5 (or_5_out, or_4_out, in[5]);
  or or_6 (or_6_out, or_5_out, in[6]);
  or or_7 (out, or_6_out, in[7]);
endmodule

module DMux8Way (
  input  [2:0] in_1,
  input  in,
  output a,
  output b,
  output c,
  output d,
  output e,
  output f,
  output g,
  output h
);

  Demultiplexer #(.select(3), .enable("false")) demultiplexer_1 (
    .out0(a), .out1(b), .out2(c), .out3(d), .out4(e), .out5(f), .out6(g), .out7(h), .in(in), .sel(in_1));
endmodule

module Mux4Way16 (
  input  [15:0] a,
  input  [15:0] b,
  input  [15:0] c,
  input  [1:0] sel,
  input  [15:0] d,
  output [15:0] out
);

  Multiplexer #(.select(2), .width(16), .enable("false")) multiplexer_1 (
    .in0(a), .in1(b), .in2(c), .in3(d), .out(out), .sel(sel));
endmodule

module Mux8Way16 (
  input  [15:0] a,
  input  [15:0] b,
  input  [15:0] c,
  input  [15:0] d,
  input  [15:0] e,
  input  [15:0] f,
  input  [2:0] sel,
  input  [15:0] g,
  input  [15:0] h,
  output [15:0] out
);

  Multiplexer #(.select(3), .width(16), .enable("false")) multiplexer_1 (
    .in0(a), .in1(b), .in2(c), .in3(d), .in4(e), .in5(f), .in6(g), .in7(h), .out(out), .sel(sel));
endmodule

module ALU (
  input  zx,
  input  nx,
  input  zy,
  input  ny,
  input  f,
  input  no,
  input  [15:0] x,
  input  [15:0] y,
  output [15:0] out,
  output zr,
  output ng
);

  wire Or8Way_2_out, Or8Way_out, or_1_out;
  wire [15:0] Add16_out, And16_out, Mux16_2_out, Mux16_3_out, Mux16_4_out, Mux16_5_out, Mux16_out,
       Not16_2_out, Not16_3_out, Not16_out;

  Mux16 Mux16 (.a(x), .b({16{1'b0}}), .out(Mux16_out), .sel(zx));
  Not16 Not16 (.out(Not16_out), .in(Mux16_out));
  Mux16 Mux16_2 (.a(y), .b({16{1'b0}}), .out(Mux16_2_out), .sel(zy));
  Not16 Not16_2 (.out(Not16_2_out), .in(Mux16_2_out));
  Mux16 Mux16_3 (.a(Mux16_out), .b(Not16_out), .out(Mux16_3_out), .sel(nx));
  Mux16 Mux16_4 (.a(Mux16_2_out), .b(Not16_2_out), .out(Mux16_4_out), .sel(ny));
  And16 And16 (.out(And16_out), .a(Mux16_3_out), .b(Mux16_4_out));
  Add16 Add16 (.In_A(Mux16_3_out), .In_B(Mux16_4_out), .Out(Add16_out));
  Mux16 Mux16_5 (.a(And16_out), .b(Add16_out), .out(Mux16_5_out), .sel(f));
  Not16 Not16_3 (.out(Not16_3_out), .in(Mux16_5_out));
  Mux16 Mux16_6 (.a(Mux16_5_out), .b(Not16_3_out), .out({ng, out[14:0]}), .sel(no));
  Or8Way Or8Way (.in(out[7:0]), .out(Or8Way_out));
  Or8Way Or8Way_2 (.in({ng, out[14:8]}), .out(Or8Way_2_out));
  not not_1 (zr, or_1_out);
  or or_1 (or_1_out, Or8Way_2_out, Or8Way_out);

  assign out[15] = ng;
endmodule

module DFF_Classic (
  input  d,
  output q1,
  output q2
);

  wire clock_1_out, nand_1_out, nand_2_out, nand_3_out;

  Clock clock_1 (.out(clock_1_out));
  nand nand_1 (nand_1_out, d, d);
  nand nand_2 (nand_2_out, d, clock_1_out);
  nand nand_3 (nand_3_out, clock_1_out, nand_1_out);
  nand nand_4 (q1, nand_2_out, q2);
  nand nand_5 (q2, q1, nand_3_out);
endmodule

module Bit (
  input  load,
  input  in,
  input  clk,
  output out
);

  wire DFF_out;

  DFF DFF (.in(out), .clk(clk), .out(DFF_out));
  Multiplexer #(.enable("false")) multiplexer_1 (.in0(DFF_out), .in1(in), .out(out), .sel(load));
endmodule

module DFF (
  input  in,
  input  clk,
  output out
);

  wire nand_1_out, nand_2_out, nand_3_out, nand_5_out;

  nand nand_1 (nand_1_out, in, in);
  nand nand_2 (nand_2_out, in, clk);
  nand nand_3 (nand_3_out, clk, nand_1_out);
  nand nand_4 (out, nand_2_out, nand_5_out);
  nand nand_5 (nand_5_out, out, nand_3_out);
endmodule

module Register (
  input  load,
  input  [15:0] in,
  input  clk,
  output [15:0] out
);

  Bit Bit (.in(in[0]), .out(out[0]), .load(load), .clk(clk));
  Bit Bit_2 (.in(in[1]), .out(out[1]), .load(load), .clk(clk));
  Bit Bit_3 (.in(in[2]), .out(out[2]), .load(load), .clk(clk));
  Bit Bit_4 (.in(in[3]), .out(out[3]), .load(load), .clk(clk));
  Bit Bit_5 (.in(in[5]), .out(out[5]), .load(load), .clk(clk));
  Bit Bit_6 (.in(in[4]), .out(out[4]), .load(load), .clk(clk));
  Bit Bit_7 (.in(in[7]), .out(out[7]), .load(load), .clk(clk));
  Bit Bit_8 (.in(in[6]), .out(out[6]), .load(load), .clk(clk));
  Bit Bit_9 (.in(in[9]), .out(out[9]), .load(load), .clk(clk));
  Bit Bit_10 (.in(in[8]), .out(out[8]), .load(load), .clk(clk));
  Bit Bit_11 (.in(in[10]), .out(out[10]), .load(load), .clk(clk));
  Bit Bit_12 (.in(in[11]), .out(out[11]), .load(load), .clk(clk));
  Bit Bit_13 (.in(in[13]), .out(out[13]), .load(load), .clk(clk));
  Bit Bit_14 (.in(in[12]), .out(out[12]), .load(load), .clk(clk));
  Bit Bit_15 (.in(in[15]), .out(out[15]), .load(load), .clk(clk));
  Bit Bit_16 (.in(in[14]), .out(out[14]), .load(load), .clk(clk));
endmodule

module RAM8 (
  input  load,
  input  [15:0] in,
  input  [2:0] address,
  input  clk,
  output [15:0] out
);

  wire DMux8Way_a, DMux8Way_b, DMux8Way_c, DMux8Way_d, DMux8Way_e, DMux8Way_f, DMux8Way_g, DMux8Way_h;
  wire [15:0] Register_2_out, Register_3_out, Register_4_out, Register_5_out, Register_6_out, Register_7_out,
       Register_8_out, Register_out;

  DMux8Way DMux8Way (
    .in(load), .in_1(address), .a(DMux8Way_a), .b(DMux8Way_b), .c(DMux8Way_c), .d(DMux8Way_d),
    .e(DMux8Way_e), .f(DMux8Way_f), .g(DMux8Way_g), .h(DMux8Way_h));
  Register Register (.out(Register_out), .in(in), .load(DMux8Way_a), .clk(clk));
  Register Register_2 (.out(Register_2_out), .in(in), .load(DMux8Way_b), .clk(clk));
  Register Register_3 (.out(Register_3_out), .in(in), .load(DMux8Way_c), .clk(clk));
  Register Register_4 (.out(Register_4_out), .in(in), .load(DMux8Way_d), .clk(clk));
  Register Register_5 (.out(Register_5_out), .in(in), .load(DMux8Way_e), .clk(clk));
  Register Register_6 (.out(Register_6_out), .in(in), .load(DMux8Way_g), .clk(clk));
  Register Register_7 (.out(Register_7_out), .in(in), .load(DMux8Way_f), .clk(clk));
  Register Register_8 (.out(Register_8_out), .in(in), .load(DMux8Way_h), .clk(clk));
  Mux8Way16 Mux8Way16 (
    .a(Register_out), .b(Register_2_out), .c(Register_3_out), .d(Register_4_out), .e(Register_5_out),
    .f(Register_7_out), .g(Register_6_out), .h(Register_8_out), .sel(address), .out(out));
endmodule

module RAM64 (
  input  load,
  input  [15:0] in,
  input  [5:0] address,
  output [15:0] out
);

  wire clock_1_out, demultiplexer_1_out0, demultiplexer_1_out1, demultiplexer_1_out2, demultiplexer_1_out3,
       demultiplexer_1_out4, demultiplexer_1_out5, demultiplexer_1_out6, demultiplexer_1_out7;
  wire [15:0] ram_1_data, ram_2_data, ram_3_data, ram_4_data, ram_5_data, ram_6_data, ram_7_data, ram_8_data;

  Demultiplexer #(.select(3), .enable("false")) demultiplexer_1 (
    .out0(demultiplexer_1_out0), .out1(demultiplexer_1_out1), .out2(demultiplexer_1_out2),
    .out3(demultiplexer_1_out3), .out4(demultiplexer_1_out4), .out5(demultiplexer_1_out5),
    .out6(demultiplexer_1_out6), .out7(demultiplexer_1_out7), .in(load), .sel(address[2:0]));
  Clock clock_1 (.out(clock_1_out));
  RAM #(.addrWidth(3), .dataWidth(16), .bus("separate")) ram_1 (
    .addr(address[5:3]), .din(in), .data(ram_1_data), .str(demultiplexer_1_out0), .clk(clock_1_out));  // open: sel, ld, clr
  RAM #(.addrWidth(3), .dataWidth(16), .bus("separate")) ram_2 (
    .addr(address[5:3]), .din(in), .data(ram_2_data), .str(demultiplexer_1_out1), .clk(clock_1_out));  // open: sel, ld, clr
  RAM #(.addrWidth(3), .dataWidth(16), .bus("separate")) ram_3 (
    .addr(address[5:3]), .din(in), .data(ram_3_data), .str(demultiplexer_1_out2), .clk(clock_1_out));  // open: sel, ld, clr
  RAM #(.addrWidth(3), .dataWidth(16), .bus("separate")) ram_4 (
    .addr(address[5:3]), .din(in), .data(ram_4_data), .str(demultiplexer_1_out3), .clk(clock_1_out));  // open: sel, ld, clr
  RAM #(.addrWidth(3), .dataWidth(16), .bus("separate")) ram_5 (
    .addr(address[5:3]), .din(in), .data(ram_5_data), .str(demultiplexer_1_out4), .clk(clock_1_out));  // open: sel, ld, clr
  RAM #(.addrWidth(3), .dataWidth(16), .bus("separate")) ram_6 (
    .addr(address[5:3]), .din(in), .data(ram_6_data), .str(demultiplexer_1_out5), .clk(clock_1_out));  // open: sel, ld, clr
  RAM #(.addrWidth(3), .dataWidth(16), .bus("separate")) ram_7 (
    .addr(address[5:3]), .din(in), .data(ram_7_data), .str(demultiplexer_1_out6), .clk(clock_1_out));  // open: sel, ld, clr
  RAM #(.addrWidth(3), .dataWidth(16), .bus("separate")) ram_8 (
    .addr(address[5:3]), .din(in), .data(ram_8_data), .str(demultiplexer_1_out7), .clk(clock_1_out));  // open: sel, ld, clr
  Multiplexer #(.select(3), .width(16), .enable("false")) multiplexer_1 (
    .in0(ram_1_data), .in1(ram_2_data), .in2(ram_3_data), .in3(ram_4_data), .in4(ram_5_data),
    .in5(ram_6_data), .in6(ram_7_data), .in7(ram_8_data), .out(out), .sel(address[2:0]));
endmodule

module RAM512 (
  input  load,
  input  [15:0] in,
  input  [8:0] address,
  output [15:0] out
);

  wire clock_1_out, demultiplexer_1_out0, demultiplexer_1_out1, demultiplexer_1_out2, demultiplexer_1_out3,
       demultiplexer_1_out4, demultiplexer_1_out5, demultiplexer_1_out6, demultiplexer_1_out7;
  wire [15:0] ram_1_data, ram_2_data, ram_3_data, ram_4_data, ram_5_data, ram_6_data, ram_7_data, ram_8_data;

  Demultiplexer #(.select(3), .enable("false")) demultiplexer_1 (
    .out0(demultiplexer_1_out0), .out1(demultiplexer_1_out1), .out2(demultiplexer_1_out2),
    .out3(demultiplexer_1_out3), .out4(demultiplexer_1_out4), .out5(demultiplexer_1_out5),
    .out6(demultiplexer_1_out6), .out7(demultiplexer_1_out7), .in(load), .sel(address[2:0]));
  Clock clock_1 (.out(clock_1_out));
  RAM #(.addrWidth(6), .dataWidth(16), .bus("separate")) ram_1 (
    .addr(address[8:3]), .din(in), .data(ram_1_data), .str(demultiplexer_1_out0), .clk(clock_1_out));  // open: sel, ld, clr
  RAM #(.addrWidth(6), .dataWidth(16), .bus("separate")) ram_2 (
    .addr(address[8:3]), .din(in), .data(ram_2_data), .str(demultiplexer_1_out1), .clk(clock_1_out));  // open: sel, ld, clr
  RAM #(.addrWidth(6), .dataWidth(16), .bus("separate")) ram_3 (
    .addr(address[8:3]), .din(in), .data(ram_3_data), .str(demultiplexer_1_out2), .clk(clock_1_out));  // open: sel, ld, clr
  RAM #(.addrWidth(6), .dataWidth(16), .bus("separate")) ram_4 (
    .addr(address[8:3]), .din(in), .data(ram_4_data), .str(demultiplexer_1_out3), .clk(clock_1_out));  // open: sel, ld, clr
  RAM #(.addrWidth(6), .dataWidth(16), .bus("separate")) ram_5 (
    .addr(address[8:3]), .din(in), .data(ram_5_data), .str(demultiplexer_1_out4), .clk(clock_1_out));  // open: sel, ld, clr
  RAM #(.addrWidth(6), .dataWidth(16), .bus("separate")) ram_6 (
    .addr(address[8:3]), .din(in), .data(ram_6_data), .str(demultiplexer_1_out5), .clk(clock_1_out));  // open: sel, ld, clr
  RAM #(.addrWidth(6), .dataWidth(16), .bus("separate")) ram_7 (
    .addr(address[8:3]), .din(in), .data(ram_7_data), .str(demultiplexer_1_out6), .clk(clock_1_out));  // open: sel, ld, clr
  RAM #(.addrWidth(6), .dataWidth(16), .bus("separate")) ram_8 (
    .addr(address[8:3]), .din(in), .data(ram_8_data), .str(demultiplexer_1_out7), .clk(clock_1_out));  // open: sel, ld, clr
  Multiplexer #(.select(3), .width(16), .enable("false")) multiplexer_1 (
    .in0(ram_1_data), .in1(ram_2_data), .in2(ram_3_data), .in3(ram_4_data), .in4(ram_5_data),
    .in5(ram_6_data), .in6(ram_7_data), .in7(ram_8_data), .out(out), .sel(address[2:0]));
endmodule

module RAM4K (
  input  load,
  input  [15:0] in,
  input  [11:0] address,
  output [15:0] out
);

  wire clock_1_out, demultiplexer_1_out0, demultiplexer_1_out1, demultiplexer_1_out2, demultiplexer_1_out3,
       demultiplexer_1_out4, demultiplexer_1_out5, demultiplexer_1_out6, demultiplexer_1_out7;
  wire [15:0] ram_1_data, ram_2_data, ram_3_data, ram_4_data, ram_5_data, ram_6_data, ram_7_data, ram_8_data;

  Demultiplexer #(.select(3), .enable("false")) demultiplexer_1 (
    .out0(demultiplexer_1_out0), .out1(demultiplexer_1_out1), .out2(demultiplexer_1_out2),
    .out3(demultiplexer_1_out3), .out4(demultiplexer_1_out4), .out5(demultiplexer_1_out5),
    .out6(demultiplexer_1_out6), .out7(demultiplexer_1_out7), .in(load), .sel(address[2:0]));
  Clock clock_1 (.out(clock_1_out));
  RAM #(.addrWidth(9), .dataWidth(16), .bus("separate")) ram_1 (
    .addr(address[11:3]), .din(in), .data(ram_1_data), .str(demultiplexer_1_out0), .clk(clock_1_out));  // open: sel, ld, clr
  RAM #(.addrWidth(9), .dataWidth(16), .bus("separate")) ram_2 (
    .addr(address[11:3]), .din(in), .data(ram_2_data), .str(demultiplexer_1_out1), .clk(clock_1_out));  // open: sel, ld, clr
  RAM #(.addrWidth(9), .dataWidth(16), .bus("separate")) ram_3 (
    .addr(address[11:3]), .din(in), .data(ram_3_data), .str(demultiplexer_1_out2), .clk(clock_1_out));  // open: sel, ld, clr
  RAM #(.addrWidth(9), .dataWidth(16), .bus("separate")) ram_4 (
    .addr(address[11:3]), .din(in), .data(ram_4_data), .str(demultiplexer_1_out3), .clk(clock_1_out));  // open: sel, ld, clr
  RAM #(.addrWidth(9), .dataWidth(16), .bus("separate")) ram_5 (
    .addr(address[11:3]), .din(in), .data(ram_5_data), .str(demultiplexer_1_out4), .clk(clock_1_out));  // open: sel, ld, clr
  RAM #(.addrWidth(9), .dataWidth(16), .bus("separate")) ram_6 (
    .addr(address[11:3]), .din(in), .data(ram_6_data), .str(demultiplexer_1_out5), .clk(clock_1_out));  // open: sel, ld, clr
  RAM #(.addrWidth(9), .dataWidth(16), .bus("separate")) ram_7 (
    .addr(address[11:3]), .din(in), .data(ram_7_data), .str(demultiplexer_1_out6), .clk(clock_1_out));  // open: sel, ld, clr
  RAM #(.addrWidth(9), .dataWidth(16), .bus("separate")) ram_8 (
    .addr(address[11:3]), .din(in), .data(ram_8_data), .str(demultiplexer_1_out7), .clk(clock_1_out));  // open: sel, ld, clr
  Multiplexer #(.select(3), .width(16), .enable("false")) multiplexer_1 (
    .in0(ram_1_data), .in1(ram_2_data), .in2(ram_3_data), .in3(ram_4_data), .in4(ram_5_data),
    .in5(ram_6_data), .in6(ram_7_data), .in7(ram_8_data), .out(out), .sel(address[2:0]));
endmodule

module RAM16K (
  input  load,
  input  [15:0] in,
  input  [13:0] address,
  output [15:0] out
);

  wire clock_1_out, demultiplexer_1_out0, demultiplexer_1_out1, demultiplexer_1_out2, demultiplexer_1_out3;
  wire [15:0] ram_1_data, ram_2_data, ram_3_data, ram_4_data;

  Clock clock_1 (.out(clock_1_out));
  Demultiplexer #(.select(2), .enable("false")) demultiplexer_1 (
    .out0(demultiplexer_1_out0), .out1(demultiplexer_1_out1), .out2(demultiplexer_1_out2),
    .out3(demultiplexer_1_out3), .in(load), .sel(address[1:0]));
  RAM #(.addrWidth(12), .dataWidth(16), .bus("separate")) ram_1 (
    .addr(address[13:2]), .din(in), .data(ram_1_data), .str(demultiplexer_1_out0), .clk(clock_1_out));  // open: sel, ld, clr
  RAM #(.addrWidth(12), .dataWidth(16), .bus("separate")) ram_2 (
    .addr(address[13:2]), .din(in), .data(ram_2_data), .str(demultiplexer_1_out1), .clk(clock_1_out));  // open: sel, ld, clr
  RAM #(.addrWidth(12), .dataWidth(16), .bus("separate")) ram_3 (
    .addr(address[13:2]), .din(in), .data(ram_3_data), .str(demultiplexer_1_out2), .clk(clock_1_out));  // open: sel, ld, clr
  RAM #(.addrWidth(12), .dataWidth(16), .bus("separate")) ram_4 (
    .addr(address[13:2]), .din(in), .data(ram_4_data), .str(demultiplexer_1_out3), .clk(clock_1_out));  // open: sel, ld, clr
  Multiplexer #(.select(2), .width(16), .enable("false")) multiplexer_1 (
    .in0(ram_1_data), .in1(ram_2_data), .in2(ram_3_data), .in3(ram_4_data), .out(out), .sel(address[1:0]));
endmodule

module PC (
  input  inc,
  input  load,
  input  reset,
  input  [15:0] in,
  output [15:0] out
);

  wire clock_1_out;
  wire [15:0] adder_1_out, buffer_1_out, multiplexer_1_out, multiplexer_2_out, multiplexer_3_out;

  Register Register (.out(out), .in(buffer_1_out), .load(1'b1), .clk(clock_1_out));
  Clock clock_1 (.out(clock_1_out));
  Adder #(.width(16)) adder_1 (.a(out), .b({16{1'b1}}), .out(adder_1_out));  // open: cin, cout
  Multiplexer #(.width(16), .enable("false")) multiplexer_1 (
    .in0(out), .in1(adder_1_out), .out(multiplexer_1_out), .sel(inc));
  Multiplexer #(.width(16), .enable("false")) multiplexer_2 (
    .in0(multiplexer_1_out), .in1(in), .out(multiplexer_2_out), .sel(load));
  assign buffer_1_out = multiplexer_3_out;  // Buffer buffer_1, 16 bits wide
  Multiplexer #(.width(16), .enable("false")) multiplexer_3 (
    .in0(multiplexer_2_out), .in1({16{1'b0}}), .out(multiplexer_3_out), .sel(reset));
endmodule

module TEST (
  input  in_1,
  input  in_2,
  input  [15:0] in_3,
  input  in_4,
  input  [2:0] in_5,
  output [15:0] out_6,
  output out_7
);

  wire clock_1_out;

  Bit Bit (.in(in_4), .out(out_7), .load(in_2), .clk(clock_1_out));
  Clock clock_1 (.out(clock_1_out));
  RAM8 RAM8 (.address(in_5), .in(in_3), .out(out_6), .load(in_1), .clk(clock_1_out));
endmodule

module PC_2 (
  input  inc,
  input  load,
  input  reset,
  input  [15:0] in,
  output [15:0] out
);

  wire and_1_out, clock_1_out, or_1_out;
  wire [15:0] and_2_out, bit_extender_1_out;

  or or_1 (or_1_out, reset, load);
  assign bit_extender_1_out = {{15{reset}}, reset};  // Bit_Extender bit_extender_1
  Counter #(.width(16), .max('hffff)) counter_1 (
    .load(or_1_out), .D(and_2_out), .count(and_1_out), .Q(out), .clk(clock_1_out));  // open: carry, clr
  and and_1 (and_1_out, ~or_1_out, inc);  // AND_Gate
  Clock clock_1 (.out(clock_1_out));
  assign and_2_out = ~bit_extender_1_out & in;  // AND_Gate and_2, 16 bits wide
endmodule
