// Logisim project HACK_Screen.circ as structural Verilog: 4 circuits, main circuit Computer
module Computer (
  input  reset
);

  wire and_1_out, clk, d_ff_1_q, decoder_1_out0, decoder_1_out1, selKBD, selRAM, selSCR, writeM;
  wire [6:0] keyboard_1_data;
  wire [14:0] addrM, cpu_1_pc;
  wire [15:0] hack_video_display_1_p6, inM, outM, rom_1_data;
  wire [15:15] keyboard_1_avail;

  Decoder #(.select(2), .enable("false")) decoder_1 (
    .out0(decoder_1_out0), .out1(decoder_1_out1), .out2(selSCR), .out3(selKBD), .sel(addrM[14:13]));
  // Probe on inM
  ROM #(.addrWidth(15), .dataWidth(16)) rom_1 (.addr(cpu_1_pc), .data(rom_1_data), .sel(1'b1));
  or or_1 (selRAM, decoder_1_out0, decoder_1_out1);
  CPU cpu_1 (
    .instruction(rom_1_data), .inM(inM), .reset(reset), .outM(outM), .writeM(writeM), .addressM(addrM),
    .pc(cpu_1_pc), .clk(clk));
  RAM #(.addrWidth(14), .dataWidth(16), .bus("separate")) ram_1 (
    .addr(addrM[13:0]), .din(outM), .data(inM), .str(writeM), .sel(selRAM), .clk(clk), .ld(1'b1), .clr(1'b0));
  // Probe on outM
  // Probe on addrM
  // Probe on cpu_1_pc
  and and_1 (and_1_out, selSCR, writeM);
  Keyboard keyboard_1 (.clk(d_ff_1_q), .re(selKBD), .clr(reset), .avail(keyboard_1_avail[15]), .data(keyboard_1_data));
  D_Flip_Flop d_ff_1 (.clk(clk), .D(writeM), .Q(d_ff_1_q));  // open: Qn, preset, en, reset
  assign inM = selSCR ? hack_video_display_1_p6 : 16'bz;  // Controlled_Buffer controlled_buffer_1
  // HACK_Video_Display hack_video_display_1: pin names not known; wires that end beside it: reset, clk, and_1_out, addrM[12:0], outM, hack_video_display_1_p6
  assign inM = selKBD ? {keyboard_1_avail[15], {8{1'b0}}, keyboard_1_data} : 16'bz;  // Controlled_Buffer controlled_buffer_2

  // Notes on the sheet:
  //   ROM
  //   CPU
  //   contents of rom_1 (hex, n*v repeats v):
  //   64 ec10 10 e308 11 efc8 11 fc10 10 fc20 e308 10 fdc8 11 fc10 f098 6 e305 2 ec10 12 e308 13 e308 4000
  //   ec10 1010 e090 14 e308 10 ea88 11 efc8 13 fc10 15 e308 11 fc10 14 fc20 f548 10 fdc8 11 f098 37 e305
  //   14 fdc8 10 ea88 11 efc8 15 fc98 26 e305 12 fc10 13 f088 13 fc10 15 e308 11 fc10 14 fc20 f548 20 ec10
  //   14 f1d8 4000 e4d0 96 e304 15 fc98 43 e305 12 fc10 13 f088 13 fc10 15 e308 11 fc10 14 fc20 f548 10
  //   fc98 6b e303 14 fc88 f ec10 10 e308 10 fc10 64 e0a0 fc10 11 e308 15 fc98 5c e305 12 fc10 13 f088 13
  //   fc10 15 e308 11 fc10 14 fc20 f548 20 ec10 14 f098 6000 e4d0 96 e303 15 fc98 7e e305 12 fc10 13 f088
  //   22 ea87 96 ea87
  //   Keyboard
endmodule

module CPU (
  input  [15:0] instruction,
  input  [15:0] inM,
  input  reset,
  output [15:0] outM,
  output writeM,
  output [14:0] addressM,
  output [14:0] pc,
  output clk
);

  wire [15:0] c, D_Register_out, mux16_1_out, mux16_2_out;
  wire [15:15] A_Register_out, pc_1_out;

  Decode decode_1 (.inst(instruction), .ctrl_in({c[15:4], writeM, c[2:0]}), .ctrl_out({c[15:4], writeM, c[2:0]}));
  Clock clock_1 (.out(clk));
  Mux16 mux16_1 (.a(outM), .b(instruction), .out(mux16_1_out), .sel(c[15]));  // open: sel_2
  Register D_Register (.in(outM), .out(D_Register_out), .load(c[4]));
  Register A_Register (.in(mux16_1_out), .out({A_Register_out[15], addressM}), .load(c[5]));
  Mux16 mux16_2 (.a({A_Register_out[15], addressM}), .b(inM), .out(mux16_2_out), .sel(c[12]));  // open: sel_2
  PC pc_1 (.in({A_Register_out[15], addressM}), .out({pc_1_out[15], pc}), .inc(c[14]), .load(c[0]), .reset(reset));
  ALU alu_1 (
    .x(D_Register_out), .y(mux16_2_out), .out(outM), .zx(c[11]), .nx(c[10]), .zy(c[9]), .ny(c[8]), .f(c[7]),
    .no(c[6]), .zr(c[1]), .ng(c[2]));

  // Other names for the same wires on the sheet: c[3] = writeM

  // Notes on the sheet:
  //   Use control-T to toggle system clock.
  //   Clock for Computer's I/O circuits
  //   Don't click on this!
endmodule

module Decode (
  input  [15:0] inst,
  input  [15:0] ctrl_in,
  output [15:0] ctrl_out
);

  wire [1:0] and_1_out;
  wire [1:1] power_on_reset_1_por;
  wire [2:1] mux8way16_1_out;

  Power_on_Reset power_on_reset_1 (.POR(power_on_reset_1_por[1]));
  Mux8Way16 mux8way16_1 (
    .a(16'hc020), .b(16'hc020), .c(16'hc020), .d(16'hc020), .e({2'b01, inst[13:3], 2'b00, inst[0]}),
    .f({2'b01, inst[13:3], 2'b00, inst[1]}), .g({2'b01, inst[13:3], 2'b00, inst[2]}),
    .h({2'b01, inst[13:3], 3'b000}), .out({ctrl_out[15:3], mux8way16_1_out, ctrl_out[0]}),
    .sel_2({inst[15], and_1_out}));  // open: sel
  assign and_1_out = ctrl_in[2:1] & ~{2{power_on_reset_1_por[1]}};  // AND_Gate and_1, 2 bits wide

  // Notes on the sheet:
  //   This instruction decoder shows the power of multiplexors.
  //   This decoder cannot be used in the N2T Hardware Simulator
  //   because it is used in an asynchronous feedback loop.
  //   This feedback loop requires a Power-on Reset circuit due to
  //   a slight bug in how Logisim's Multiplexor handles "unknown"
  //   select inputs.  If any select bit is unknown, all output bits are
  //   errors, even if the input values are such that the output bit
  //   is determined regardless of the unknown select bits' values.
endmodule

module Power_on_Reset (
  output POR
);

  wire buffer_1_out, buffer_2_out, buffer_3_out, buffer_4_out, buffer_5_out, buffer_6_out, buffer_7_out,
       buffer_8_out, buffer_9_out, buffer_10_out, buffer_11_out, buffer_12_out, buffer_13_out, buffer_14_out,
       buffer_15_out, buffer_16_out, buffer_17_out, buffer_18_out, buffer_19_out, buffer_20_out,
       buffer_21_out, buffer_22_out, buffer_23_out, buffer_24_out, buffer_25_out, buffer_26_out,
       buffer_27_out, buffer_28_out, buffer_29_out, buffer_30_out, buffer_31_out, buffer_32_out,
       buffer_33_out, buffer_34_out, buffer_35_out, buffer_36_out, buffer_37_out, buffer_38_out,
       buffer_39_out, buffer_40_out, buffer_41_out, buffer_42_out, buffer_43_out, buffer_44_out,
       buffer_45_out, buffer_46_out, buffer_47_out, buffer_48_out, buffer_49_out, buffer_50_out,
       buffer_51_out, buffer_52_out, buffer_53_out, buffer_54_out, buffer_55_out, buffer_56_out,
       buffer_57_out, buffer_58_out, buffer_59_out, buffer_60_out, buffer_61_out, buffer_62_out,
       buffer_63_out, buffer_64_out, buffer_65_out, buffer_66_out, buffer_67_out, buffer_68_out,
       buffer_69_out, buffer_70_out, buffer_71_out, buffer_72_out, buffer_73_out, buffer_74_out,
       buffer_75_out, buffer_76_out, buffer_77_out, buffer_78_out, buffer_79_out, buffer_80_out,
       buffer_81_out, buffer_82_out, buffer_83_out, buffer_84_out, buffer_85_out, buffer_86_out,
       buffer_87_out, buffer_88_out, buffer_89_out, buffer_90_out, buffer_91_out, buffer_92_out,
       buffer_93_out, buffer_94_out, buffer_95_out, buffer_96_out, buffer_97_out, buffer_98_out,
       buffer_99_out;

  buf buffer_1 (buffer_1_out, 1'b0);
  buf buffer_2 (buffer_2_out, buffer_91_out);
  buf buffer_3 (buffer_3_out, buffer_92_out);
  buf buffer_4 (buffer_4_out, buffer_93_out);
  buf buffer_5 (buffer_5_out, buffer_94_out);
  buf buffer_6 (buffer_6_out, buffer_95_out);
  buf buffer_7 (buffer_7_out, buffer_96_out);
  buf buffer_8 (buffer_8_out, buffer_97_out);
  buf buffer_9 (buffer_9_out, buffer_98_out);
  buf buffer_10 (buffer_10_out, buffer_99_out);
  buf buffer_11 (buffer_11_out, buffer_14_out);
  buf buffer_12 (buffer_12_out, buffer_1_out);
  buf buffer_13 (buffer_13_out, buffer_12_out);
  buf buffer_14 (buffer_14_out, buffer_13_out);
  buf buffer_15 (buffer_15_out, buffer_16_out);
  buf buffer_16 (buffer_16_out, buffer_2_out);
  buf buffer_17 (buffer_17_out, buffer_18_out);
  buf buffer_18 (buffer_18_out, buffer_15_out);
  buf buffer_19 (buffer_19_out, buffer_3_out);
  buf buffer_20 (buffer_20_out, buffer_22_out);
  buf buffer_21 (buffer_21_out, buffer_19_out);
  buf buffer_22 (buffer_22_out, buffer_21_out);
  buf buffer_23 (buffer_23_out, buffer_26_out);
  buf buffer_24 (buffer_24_out, buffer_23_out);
  buf buffer_25 (buffer_25_out, buffer_4_out);
  buf buffer_26 (buffer_26_out, buffer_25_out);
  buf buffer_27 (buffer_27_out, buffer_28_out);
  buf buffer_28 (buffer_28_out, buffer_30_out);
  buf buffer_29 (buffer_29_out, buffer_27_out);
  buf buffer_30 (buffer_30_out, buffer_5_out);
  buf buffer_31 (buffer_31_out, buffer_33_out);
  buf buffer_32 (buffer_32_out, buffer_6_out);
  buf buffer_33 (buffer_33_out, buffer_32_out);
  buf buffer_34 (buffer_34_out, buffer_31_out);
  buf buffer_35 (buffer_35_out, buffer_7_out);
  buf buffer_36 (buffer_36_out, buffer_37_out);
  buf buffer_37 (buffer_37_out, buffer_38_out);
  buf buffer_38 (buffer_38_out, buffer_35_out);
  buf buffer_39 (buffer_39_out, buffer_42_out);
  buf buffer_40 (buffer_40_out, buffer_8_out);
  buf buffer_41 (buffer_41_out, buffer_40_out);
  buf buffer_42 (buffer_42_out, buffer_41_out);
  buf buffer_43 (buffer_43_out, buffer_45_out);
  buf buffer_44 (buffer_44_out, buffer_46_out);
  buf buffer_45 (buffer_45_out, buffer_9_out);
  buf buffer_46 (buffer_46_out, buffer_43_out);
  buf buffer_47 (buffer_47_out, buffer_10_out);
  buf buffer_48 (buffer_48_out, buffer_50_out);
  buf buffer_49 (buffer_49_out, buffer_47_out);
  buf buffer_50 (buffer_50_out, buffer_49_out);
  buf buffer_51 (buffer_51_out, buffer_52_out);
  buf buffer_52 (buffer_52_out, buffer_54_out);
  buf buffer_53 (buffer_53_out, buffer_11_out);
  buf buffer_54 (buffer_54_out, buffer_53_out);
  buf buffer_55 (buffer_55_out, buffer_57_out);
  buf buffer_56 (buffer_56_out, buffer_58_out);
  buf buffer_57 (buffer_57_out, buffer_56_out);
  buf buffer_58 (buffer_58_out, buffer_17_out);
  buf buffer_59 (buffer_59_out, buffer_61_out);
  buf buffer_60 (buffer_60_out, buffer_62_out);
  buf buffer_61 (buffer_61_out, buffer_20_out);
  buf buffer_62 (buffer_62_out, buffer_59_out);
  buf buffer_63 (buffer_63_out, buffer_24_out);
  buf buffer_64 (buffer_64_out, buffer_63_out);
  buf buffer_65 (buffer_65_out, buffer_66_out);
  buf buffer_66 (buffer_66_out, buffer_64_out);
  buf buffer_67 (buffer_67_out, buffer_29_out);
  buf buffer_68 (buffer_68_out, buffer_69_out);
  buf buffer_69 (buffer_69_out, buffer_67_out);
  buf buffer_70 (buffer_70_out, buffer_68_out);
  buf buffer_71 (buffer_71_out, buffer_74_out);
  buf buffer_72 (buffer_72_out, buffer_71_out);
  buf buffer_73 (buffer_73_out, buffer_72_out);
  buf buffer_74 (buffer_74_out, buffer_34_out);
  buf buffer_75 (buffer_75_out, buffer_36_out);
  buf buffer_76 (buffer_76_out, buffer_78_out);
  buf buffer_77 (buffer_77_out, buffer_76_out);
  buf buffer_78 (buffer_78_out, buffer_75_out);
  buf buffer_79 (buffer_79_out, buffer_82_out);
  buf buffer_80 (buffer_80_out, buffer_39_out);
  buf buffer_81 (buffer_81_out, buffer_80_out);
  buf buffer_82 (buffer_82_out, buffer_81_out);
  buf buffer_83 (buffer_83_out, buffer_86_out);
  buf buffer_84 (buffer_84_out, buffer_85_out);
  buf buffer_85 (buffer_85_out, buffer_83_out);
  buf buffer_86 (buffer_86_out, buffer_44_out);
  buf buffer_87 (buffer_87_out, buffer_88_out);
  buf buffer_88 (buffer_88_out, buffer_89_out);
  buf buffer_89 (buffer_89_out, buffer_48_out);
  buf buffer_90 (buffer_90_out, buffer_87_out);
  buf buffer_91 (buffer_91_out, buffer_51_out);
  buf buffer_92 (buffer_92_out, buffer_55_out);
  buf buffer_93 (buffer_93_out, buffer_60_out);
  buf buffer_94 (buffer_94_out, buffer_65_out);
  buf buffer_95 (buffer_95_out, buffer_70_out);
  buf buffer_96 (buffer_96_out, buffer_73_out);
  buf buffer_97 (buffer_97_out, buffer_77_out);
  buf buffer_98 (buffer_98_out, buffer_79_out);
  buf buffer_99 (buffer_99_out, buffer_84_out);
  Pull_Resistor #(.pull(1)) pull_resistor_1 (.node(POR));
  buf buffer_100 (POR, buffer_90_out);

  // Notes on the sheet:
  //   This circuit supplies a 100 gate delay long "reset" pulse.
endmodule
